# Fritzing sketch wiring_diagram (saved by Fritzing 1.0.1rc)

parts:
  J1 = Basic Servo
  PWM1 = PCA9685 16x12-bit PWM Breakout
  JACK1 = 2.1mm Barrel Jack with Terminal Block
  J2 = Basic Servo
  J3 = Basic Servo
  J4 = Basic Servo
  S3 = Round Pushbutton
  S2 = Round Pushbutton
  A1 = Raspberry Pi 5

nets:
  GND: J1.gnd, PWM1.no_name_yet#501, PWM1.no_name_yet#701, PWM1.no_name_yet#1000, PWM1.no_name_yet#1001, PWM1.no_name_yet#1002, PWM1.no_name_yet#1003, JACK1.NEG, J2.gnd, J3.gnd, J4.gnd, S3.leg1, S2.leg1, A1.GND
  VCC: J1.vcc, PWM1.no_name_yet#100, PWM1.no_name_yet#101, PWM1.no_name_yet#102, PWM1.no_name_yet#103, PWM1.no_name_yet#706, JACK1.POS, J2.vcc, J3.vcc, J4.vcc
  N1: J1.pulse, PWM1.no_name_yet#1
  N2: PWM1.no_name_yet#0, J4.pulse
  N3: PWM1.no_name_yet#2, J2.pulse
  N4: PWM1.no_name_yet#3, J3.pulse
  N5: PWM1.no_name_yet#503, A1.GPIO3
  N6: PWM1.no_name_yet#504, A1.GPIO2
  N7: PWM1.no_name_yet#505, A1.3V3
  N8: S3.leg0, A1.GPIO5
  N9: S2.leg0, A1.GPIO13

notes:
  Motor Power Supply
  5V - 2A
  Left arm motor
  HDMI to LCD
  RPi 5 Power Supply
  5V - 5A
  USB to LCD and Speaker
  USB to mouse and keyboard
  Left antenna motor
  Right arm motor
  Right antenna motor
  Right button
  Left button

custom parts:
  Raspberry Pi 5: The RPi5, a faster version of the awesome Raspberry Pi4B ARM Board with 40 pin gpio.
