# Fritzing sketch wiring_diagram (saved by Fritzing 0.9.3b)
breadboards: 1

parts:
  M2 = Stepper Motor - Bipolar
  Power_plug1 = Power plug
  M1 = Stepper Motor - Bipolar
  C12 = Electrolytic Capacitor [capacitance=1000μF package="1010 [SMD, electrolytic]"]
  C13 = Electrolytic Capacitor [capacitance=1000μF package="1010 [SMD, electrolytic]"]
  Pololu_A6 = Pololu A4988 [package=SO16]
  Pololu_A7 = Pololu A4988 [package=SO16]
  Raspberry_Pi_2 = Raspberry Pi 4 [part_number=RPI-4-b]

nets:
  N1: M2.A, Pololu_A7.2B
  N2: M2.C, Pololu_A7.2A
  N3: M2.B, Pololu_A7.1A
  N4: M2.D, Pololu_A7.1B
  N5: Power_plug1.GND, C12.-, C13.-, Pololu_A6.GND#14, Pololu_A7.GND#14
  N6: Power_plug1.VCC, C12.+, C13.+, Pololu_A6.VMOT, Pololu_A7.VMOT
  N7: M1.A, Pololu_A6.2B
  N8: M1.C, Pololu_A6.2A
  N9: M1.B, Pololu_A6.1A
  N10: M1.D, Pololu_A6.1B
  N11: Pololu_A6.RESET, Raspberry_Pi_2.GPIO4
  N12: Pololu_A6.SLEEP, Raspberry_Pi_2.GPIO17
  N13: Pololu_A6.STEP, Raspberry_Pi_2.GPIO27
  N14: Pololu_A6.DIR, Raspberry_Pi_2.GPIO22
  N15: Pololu_A6.GND#8, Pololu_A7.GND#8, Raspberry_Pi_2.GND
  VDD: Pololu_A6.VDD, Pololu_A7.VDD, Raspberry_Pi_2.5V
  N16: Pololu_A7.RESET, Raspberry_Pi_2.GPIO6
  N17: Pololu_A7.SLEEP, Raspberry_Pi_2.GPIO13
  N18: Pololu_A7.STEP, Raspberry_Pi_2.GPIO19
  N19: Pololu_A7.DIR, Raspberry_Pi_2.GPIO26

notes:
  Motor Power Supply
  12V - 2A
  Decoupling capacitors
  100 uF
  Logic Power Supply
  3 - 5V
  Pan motor
  Tilt motor
  HDMI to LCD screen

custom parts:
  Pololu A4988: The A4988 stepper motor driver carrier is a breakout board for Allegro’s A4988 microstepping bipolar stepper motor driver. The driver features adjustable current limiting, overcurrent and overtemperature protection, and five different microstep resolutions (down to 1/16-step). It operates from 8 – 35 V and can deliver up to approximately 1 A per phase without a heat sink or forced air flow (it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
  Raspberry Pi 4: The RPi4, a faster version of the awesome Raspberry Pi 2 B ARM Board with 40 pin gpio. Ready for special Raspberry Pi B+ and RPi2 Hat (Hardware attached (on) top)
